// Logisim project Fibo_counter_shm.circ as structural Verilog: 1 circuit, main circuit main
module main (
  input  Start,
  input  Reset,
  input  [15:0] in_3,
  input  [15:0] in_4,
  input  [7:0] in_5
);

  wire and_1_out, and_2_out, and_3_out, and_4_out, clock_1_out, G0_q, G1_q, nor_1_out, not_1_out, not_2_out,
       or_1_out, or_2_out, xor_1_out;
  wire [1:0] and_5_out;
  wire [7:0] C_q;
  wire [15:0] adder_1_out, multiplexer_1_out, multiplexer_2_out, R1_q, R2_q;

  not not_1 (not_1_out, Start);
  and and_1 (and_1_out, G0_q, not_1_out);
  and and_2 (and_2_out, nor_1_out, G1_q);
  and and_3 (and_3_out, Start, G0_q);
  and and_4 (and_4_out, G1_q, not_2_out);
  not not_2 (not_2_out, nor_1_out);
  or or_1 (or_1_out, and_3_out, and_5_out[1]);
  or or_2 (or_2_out, and_1_out, and_2_out);
  Clock clock_1 (.out(clock_1_out));
  D_Flip_Flop G0 (.clk(clock_1_out), .D(or_2_out), .Q(G0_q), .preset(Reset));  // open: Qn, en, reset
  D_Flip_Flop G1 (.clk(clock_1_out), .D(or_1_out), .Q(G1_q), .reset(Reset));  // open: Qn, preset, en
  D_Flip_Flop G2 (.clk(clock_1_out), .D(and_4_out), .Q(and_5_out[1]), .reset(Reset));  // open: Qn, preset, en
  LED led_1 (.in(G0_q));
  and and_5 (and_5_out[0], Start, G0_q);
  LED led_2 (.in(and_5_out[1]));
  LED led_3 (.in(R2_q[14]));
  LED led_4 (.in(R2_q[15]));
  LED led_5 (.in(and_5_out[0]));
  LED led_6 (.in(and_4_out));
  LED led_7 (.in(R2_q[12]));
  LED led_8 (.in(R2_q[13]));
  LED led_9 (.in(R2_q[11]));
  LED led_10 (.in(R2_q[10]));
  xor xor_1 (xor_1_out, and_5_out[0], and_4_out);
  LED led_11 (.in(R2_q[9]));
  LED led_12 (.in(R2_q[8]));
  LED led_13 (.in(R2_q[7]));
  LED led_14 (.in(R2_q[6]));
  LED led_15 (.in(R2_q[4]));
  LED led_16 (.in(R2_q[3]));
  LED led_17 (.in(R2_q[5]));
  LED led_18 (.in(R2_q[2]));
  Multiplexer #(.select(2), .width(16), .enable("false")) multiplexer_1 (
    .in0(R2_q), .in1(in_3), .in2(adder_1_out), .in3(R2_q), .out(multiplexer_1_out), .sel(and_5_out));
  LED led_19 (.in(R2_q[0]));
  LED led_20 (.in(R2_q[1]));
  Register #(.width(16)) R2 (.D(multiplexer_1_out), .Q(R2_q), .clk(clock_1_out));  // open: en, clr
  Adder #(.width(16)) adder_1 (.a(R2_q), .b(R1_q), .out(adder_1_out));  // open: cin, cout
  LED led_21 (.in(R1_q[15]));
  LED led_22 (.in(R1_q[14]));
  Multiplexer #(.select(2), .width(16), .enable("false")) multiplexer_2 (
    .in0(R1_q), .in1(in_4), .in2(R2_q), .in3(R1_q), .out(multiplexer_2_out), .sel(and_5_out));
  LED led_23 (.in(R1_q[10]));
  LED led_24 (.in(R1_q[13]));
  LED led_25 (.in(R1_q[12]));
  LED led_26 (.in(R1_q[11]));
  Register #(.width(16)) R1 (.D(multiplexer_2_out), .Q(R1_q), .clk(clock_1_out));  // open: en, clr
  LED led_27 (.in(R1_q[9]));
  LED led_28 (.in(R1_q[7]));
  LED led_29 (.in(R1_q[6]));
  LED led_30 (.in(R1_q[8]));
  LED led_31 (.in(R1_q[3]));
  LED led_32 (.in(R1_q[5]));
  LED led_33 (.in(R1_q[2]));
  LED led_34 (.in(R1_q[4]));
  LED led_35 (.in(R1_q[0]));
  LED led_36 (.in(R1_q[1]));
  Counter C (.load(xor_1_out), .D(in_5), .count(and_4_out), .Q(C_q), .clk(clock_1_out));  // open: carry, clr
  nor nor_1 (nor_1_out, C_q[7], C_q[6], C_q[5], C_q[4], C_q[3], C_q[2], C_q[1], C_q[0]);
  LED led_37 (.in(C_q[6]));
  LED led_38 (.in(C_q[7]));
  LED led_39 (.in(C_q[2]));
  LED led_40 (.in(C_q[4]));
  LED led_41 (.in(C_q[3]));
  LED led_42 (.in(C_q[5]));
  LED led_43 (.in(C_q[0]));
  LED led_44 (.in(C_q[1]));

  // Notes on the sheet:
  //   Fibonacci Counter(One-Hot)
  //   Controller Part
  //   Zero
  //   Rules: enter R1, R2 as the first two elements of sequence(R1<R2)
  //    Enter the number up to which you want to count(output = n+2'st element of sequence)
  //   Ready
  //   Data2
  //   Change_Regs
  //   Load_Regs
  //   Decr_C
  //   Data1
  //   DataPath
  //   CounterInput
  //   Zero
endmodule
